// Digital circuit risc-v-computer.dig as structural Verilog
module risc_v_computer (
  input  clk,
  input  clk_2,
  input  in_11,
  input  [4:0] in_12,
  output [31:0] out_1,
  output [31:0] out_2,
  output [31:0] out_3,
  output [4:0] out_4,
  output [4:0] out_5,
  output [31:0] out_6,
  output [31:0] out_7,
  output [31:0] out_8,
  output [31:0] debugreg_out,
  output [31:0] out_14
);

  wire addr_compare_1_eq_out, addrflag_mem, addrflag_peripheral, addrflag_ssd, and_1_out, ard_en,
       button_2_out, c, crd_en, Cust_op, gpio_in10, gpio_out1, gpio_out2, gpio_out3, gpio_out4, gpio_out5,
       gpio_out6, gpio_out7, gpio_out8, gpio_out9, gpio_out10, int_peripheral, int_timer, jrd_en, lrd_en,
       memgpio_en, memplic_en, mip_seten, mret, nor_2_out, not_1_out, Oe_mem, Oe_memop, Oe_ssd, PC_EN,
       PC_except, PC_inited, PC_jmp, PC_jmpen, rd_en, We_mem;
  wire [3:0] storebytes_size;
  wire [4:0] driver_11_out, rd;
  wire [5:0] csr_op;
  wire [6:0] imm_7;
  wire [7:0] data_memssd, mechine_op;
  wire [8:0] jmp_op, mem_op;
  wire [11:0] Addr_csr1, imm_12;
  wire [18:0] alu_op;
  wire [19:0] imm_20;
  wire [23:0] addr_iop;
  wire [29:24] mem_addr;
  wire [31:0] Addr_except, Addr_jmp, Addr_jmpto, ard_out, crd_out, Data_csr, data_mem, data_memgpio,
       data_memplic, data_memrd, data_memrdin, Instrction_Reg_q, int_peripheralcode, jrd_out, lrd_out,
       mip_cur, mip_set, Out_csr1, Out_csr2, program_counter_1_pc_next;

  or or_1 (rd_en, jrd_en, ard_en, crd_en, lrd_en);
  or or_2 (PC_jmpen, PC_jmp, PC_except);
  assign Addr_jmpto = PC_except ? Addr_except : 32'bz;  // Driver driver_1
  not not_1 (not_1_out, PC_inited);
  assign out_2 = not_1_out ? 32'h80000000 : 32'bz;  // Driver driver_2
  assign out_6 = jrd_en ? jrd_out : 32'bz;  // Driver driver_3
  assign out_6 = ard_en ? ard_out : 32'bz;  // Driver driver_4
  assign out_6 = crd_en ? crd_out : 32'bz;  // Driver driver_5
  assign out_6 = lrd_en ? lrd_out : 32'bz;  // Driver driver_6
  program_counter program_counter_1 (
    .En(PC_EN), .Clock(c), .Addr_set(out_2), .Addr_jmp(Addr_jmpto), .En_jmp(PC_jmpen),
    .PC_next(program_counter_1_pc_next));
  and and_1 (and_1_out, PC_jmp, ~PC_except);  // And
  instruction_decoder instruction_decoder_1 (
    .Instruction_In(out_3), .EN(PC_EN), .mechie_op(mechine_op), .rd(rd), .rs1(out_4), .rs2(out_5),
    .imm_2531(imm_7), .imm_1231(imm_20), .imm_2032(imm_12), .invalid(out_14), .csr_op(csr_op),
    .jmp_op(jmp_op), .alu_op(alu_op), .SL_op(mem_op), .Cust_op(Cust_op));
  Button button_1 (.out(gpio_in10));
  assign out_1 = not_1_out ? 32'h80000004 : 32'bz;  // Driver driver_7
  assign Addr_jmpto = and_1_out ? Addr_jmp : 32'bz;  // Driver driver_8
  assign out_1 = PC_inited ? program_counter_1_pc_next : 32'bz;  // Driver driver_9
  mechine_op_unit mechine_op_unit_1 (.mechine_op(mechine_op), .mret(mret));
  Register #(.Bits(32)) Instrction_Reg (.D(out_1), .C(c), .en(PC_EN), .Q(Instrction_Reg_q));
  LED led_1 (.in(gpio_out1));
  LED led_2 (.in(gpio_out2));
  LED led_3 (.in(gpio_out3));
  LED led_4 (.in(gpio_out4));
  LED led_5 (.in(gpio_out5));
  LED led_6 (.in(gpio_out6));
  LED led_7 (.in(gpio_out7));
  LED led_8 (.in(gpio_out8));
  LED led_9 (.in(gpio_out9));
  LED led_10 (.in(gpio_out10));
  addr_compare addr_compare_1 (.Addr_in1(out_1), .Addr_in2(32'h8000011c), .Eq_out(addr_compare_1_eq_out));
  assign out_2 = PC_inited ? Instrction_Reg_q : 32'bz;  // Driver driver_10
  instuction_jump_unit instuction_jump_unit_1 (
    .jmp_op(jmp_op), .PC_cur(out_2), .PC_next(out_1), .rs1_in(out_7), .rs2_in(out_8), .Imm12_in(imm_12),
    .Imm20_in(imm_20), .Imm7_in(imm_7), .offset_5(rd), .Addr_jmp(Addr_jmp), .rd_out(jrd_out),
    .EN_out(jrd_en), .En_jmp(PC_jmp));
  cust_ctrl cust_ctrl_1 (.op_code(out_3), .cust_code(Cust_op), .Clock(c), .PC_init(PC_inited));
  csr csr_1 (
    .CSRCode_in(csr_op), .Data_in(out_7), .Csr_Addr(imm_12), .Imm5_in(out_4), .Clock(c),
    .Data_temp(Out_csr1), .En(crd_en), .Addr_csr(Addr_csr1), .Out_rd(crd_out), .Out_csr(Data_csr));
  assign c = ~1'b0 ? clk_2 : 1'bz;  // DriverInvSel driverinvsel_1
  assign driver_11_out = rd_en ? rd : 5'bz;  // Driver driver_11
  risc_v_registers risc_v_registers_1 (
    .OE_P1(out_4), .Din(out_6), .Clock(c), .WE(driver_11_out), .OE_P2(out_5), .OE_P3(in_12),
    .Output_P1(out_7), .Output_P2(out_8), .Output_P3(debugreg_out));
  memory memory_1 (
    .Addr({addrflag_peripheral, addrflag_ssd, mem_addr, addr_iop}), .Data_in(data_mem), .WE(We_mem),
    .OE(Oe_mem), .ByteSize_in(storebytes_size), .Clock(c), .Addr_PC(out_2), .OE_PC(addrflag_mem),
    .Data_out(data_memrd), .DataPC_out(out_3));
  assign c = 1'b0 ? button_2_out : 1'bz;  // Driver driver_12
  Button button_2 (.out(button_2_out));
  boot_rom boot_rom_1 (.Addr(out_2[23:0]), .En(out_2[31]), .Out_code(out_3));
  assign PC_EN = ~1'b0 ? 1'b1 : 1'bz;  // DriverInvSel driverinvsel_2
  int_except_unit int_except_unit_1 (
    .Data_csr(Data_csr), .WE_CSR(crd_en), .Addr_csrw(Addr_csr1), .Clock(c), .Addr_csr1(Addr_csr1),
    .Addr_csr2({12{1'b0}}), .Exception_code(out_14), .PC_Addr(out_2), .PC_ip(out_3), .PC_next(out_1),
    .mret(mret), .mip_in(mip_set), .mip_en(mip_seten), .Out_csr1(Out_csr1), .Out_csr2(Out_csr2),
    .En_jmp(PC_except), .Addr_jmp(Addr_except), .mip_out(mip_cur));  // open: mie_out, ecode_out, timer_en, mepc_out
  assign PC_EN = 1'b0 ? in_11 : 1'bz;  // Driver driver_13
  nor nor_1 (addrflag_mem, addrflag_peripheral, out_2[31]);
  ROM #(.AddrBits(24), .Bits(8)) Program_Rom (.A(addr_iop), .sel(Oe_ssd), .D(data_memssd));
  alu alu_1 (
    .Alu_in(alu_op), .rs1_in(out_7), .rs2_in(out_8), .Imm12_in(imm_12), .Clock(c), .rd_out(ard_out),
    .EN_out(ard_en), .InvlidOP_out(out_14));
  memory_operation_unit memory_operation_unit_1 (
    .MemOp_in(mem_op), .Data_in(data_memrdin), .rs1(out_7), .rs2(out_8), .Offset_12(imm_12),
    .Offset_7(imm_7), .Offset_5(rd), .imm_20(imm_20), .we_out(We_mem),
    .Addr_out({addrflag_peripheral, addrflag_ssd, mem_addr, addr_iop}), .Mem_out(data_mem),
    .StoreByteSize_out(storebytes_size), .oe_out(Oe_memop), .RegWE_out(lrd_en), .rd_out(lrd_out));
  PLIC plic_1 (
    .Clock(c), .TimerClock(clk), .Addr_w({addrflag_peripheral, addrflag_ssd, mem_addr, addr_iop}),
    .Data_in(data_mem), .WE(We_mem), .Addr_r1({addrflag_peripheral, addrflag_ssd, mem_addr, addr_iop}),
    .mip_in(mip_cur), .perint_code(int_peripheralcode), .Out_ra(data_memplic), .Out_en(memplic_en),
    .mip_set(mip_set), .mip_seten(mip_seten), .int_timer(int_timer), .gate_peripheral(int_peripheral));  // open: mtimcmp, mtime
  nor nor_2 (nor_2_out, addrflag_peripheral, addrflag_ssd);
  and and_2 (Oe_ssd, addrflag_ssd, Oe_memop);
  and and_3 (Oe_mem, nor_2_out, Oe_memop);
  assign data_memrdin = memplic_en ? data_memplic : 32'bz;  // Driver driver_14
  assign data_memrdin = Oe_mem ? data_memrd : 32'bz;  // Driver driver_15
  gpio gpio_1 (
    .Clock(c), .Addr_w({addrflag_peripheral, addrflag_ssd, mem_addr, addr_iop}), .Data_in(data_mem),
    .we(We_mem), .Addr_rd({addrflag_peripheral, addrflag_ssd, mem_addr, addr_iop}),
    .int_gate(int_peripheral), .GPIO1_in(1'b0), .GPIO2_in(1'b0), .GPIO3_in(1'b0), .GPIO4_in(1'b0),
    .GPIO5_in(1'b0), .GPIO6_in(1'b0), .GPIO7_in(1'b0), .GPIO8_in(1'b0), .GPIO9_in(1'b0),
    .GPIO10_in(gpio_in10), .Out_rd(data_memgpio), .Out_en(memgpio_en), .perint_code(int_peripheralcode),
    .GPIO1_out(gpio_out1), .GPIO2_out(gpio_out2), .GPIO3_out(gpio_out3), .GPIO4_out(gpio_out4),
    .GPIO5_out(gpio_out5), .GPIO6_out(gpio_out6), .GPIO7_out(gpio_out7), .GPIO8_out(gpio_out8),
    .GPIO9_out(gpio_out9), .GPIO10_out(gpio_out10));
  assign data_memrdin = Oe_ssd ? {{24{1'b0}}, data_memssd} : 32'bz;  // Driver driver_16
  assign data_memrdin = memgpio_en ? data_memgpio : 32'bz;  // Driver driver_17

  // Other names for the same wires on the sheet: Addr_csrw[11:0] = Addr_csr1; instruction_code[31:0] = out_3;
  //   Invalid_op[31:0] = out_14; mem_addr (some bits) = {addrflag_peripheral, addrflag_ssd, addr_iop};
  //   addr_real[23:0] = out_2[23:0]; PC_exec[31:0] = out_2; addrflag_boot = out_2[31]; PC_next[31:0] = out_1;
  //   rd_out[31:0] = out_6; reg_debug[4:0] = in_12; rs1[4:0] = out_4; rs1_data[31:0] = out_7; rs2[4:0] = out_5;
  //   rs2_data[31:0] = out_8; Timer_clock = clk

  // Notes on the sheet:
  //   clk: Hz: 100
  //   clk_2: Hz: 5000
  //   Reg-Write-Bus
  //   Instruction Program Counter Bus
  //   contents of Program_Rom (hex, n*v repeats v):
  //   6*16
  //   Memory Bus
endmodule
